// Logisim project part1.circ as structural Verilog: 1 circuit, main circuit main
module main (
  input  s,
  input  x,
  input  y
);

  wire n7404_1_p3, n7408_1_p1, n7408_1_p4, n7432_1_p2;

  LED led_1 (.in(n7432_1_p2));
  // _7404 7404_1: pin names not known; wires that end beside it: 1'b0, 1'b0, n7404_1_p3, s, 1'b1
  // _7408 7408_1: pin names not known; wires that end beside it: n7408_1_p1, n7404_1_p3, x, n7408_1_p4, y, s, 1'b1
  // _7432 7432_1: pin names not known; wires that end beside it: 1'b0, n7432_1_p2, n7408_1_p1, n7408_1_p4, 1'b1

  // Notes on the sheet:
  //   Output
endmodule
