// Logisim project part2.circ as structural Verilog: 1 circuit, main circuit main
module main (
  input  a,
  input  b,
  input  c,
  input  d
);

  wire n7404_1_p2, n7404_1_p4, n7404_1_p5, n7408_1_p4, n7408_1_p7, n7408_1_p8;

  LED led_1 (.in(n7408_1_p8));
  // _7404 7404_1: pin names not known; wires that end beside it: 1'b0, n7404_1_p2, c, n7404_1_p4, n7404_1_p5, b, a, 1'b1
  // _7408 7408_1: pin names not known; wires that end beside it: c, 1'b0, 1'b0, n7408_1_p4, d, n7404_1_p4, n7408_1_p7, n7408_1_p8, n7404_1_p2, n7408_1_p4, n7404_1_p5, 1'b1, n7408_1_p7
  // _7432 7432_1: pin names not known; wires that end beside it: 1'b1

  // Notes on the sheet:
  //   output
endmodule
