// Logisim project part3.circ as structural Verilog: 1 circuit, main circuit main
module main (
  input  x,
  input  s,
  input  y
);

  wire and_1_out, and_2_out, not_1_out, or_1_out;

  not not_1 (not_1_out, s);
  and and_1 (and_1_out, x, not_1_out);
  and and_2 (and_2_out, s, y);
  or or_1 (or_1_out, and_1_out, and_2_out);
  LED led_1 (.in(or_1_out));

  // Notes on the sheet:
  //   Output
endmodule
